# Fritzing sketch Hardware system (saved by Fritzing 0.9.10b)
breadboards: 1

parts:
  HC-05_Bluetooth = Bluetooth HC-05 Macho
  J1 = Basic Servo
  uC = Arduino Uno (Rev3)

nets:
  N1: HC-05_Bluetooth.TXD, uC.D0/RX
  N2: HC-05_Bluetooth.RXD, uC.D1/TX
  VCC: HC-05_Bluetooth.VCC, J1.vcc, uC.5V
  GND: HC-05_Bluetooth.GND, J1.gnd, uC.GND
  N3: J1.pulse, uC.D9_PWM
